# Fritzing sketch rc_reset (saved by Fritzing 0.9.2b)

parts:
  Part1 = Arduino Nano (Rev3.0)
  IR_sensor = TSOP312.., 314.. [package=THT]
  RELAY = Keyes Relay [package=THT]
  POWER_SUPPLY_-_IN = Screw terminal - 2 pins [package=THT]
  POWER_SUPPLY_-_OUT = Screw terminal - 2 pins [package=THT]

nets (from the schematic view):
  N1: Part1.D7, RELAY.signal
  N2: Part1.D11/MOSI, IR_sensor.Data
  GND: Part1.VIN, Part1.GND, IR_sensor.GND, RELAY.ground, POWER_SUPPLY_-_IN.pin2, POWER_SUPPLY_-_OUT.pin1
  N3: Part1.5V, IR_sensor.Vs, RELAY.power
  N4: RELAY.NC, RELAY.C, RELAY.NO
  N5: POWER_SUPPLY_-_IN.pin1, POWER_SUPPLY_-_OUT.pin2

custom parts:
  Keyes Relay: The Keyes 5V relay module is suitable for SCM development, home appliance control. It uses a 5V~12V TIL control signal which can control DC / AC signal.
